// Logisim project Guia_1100.circ as structural Verilog: 1 circuit, main circuit main
module main (
  input  x,
  input  clk,
  output y_mealy,
  output y_moore
);

  Button reset ();  // open: out
endmodule
