// Logisim project Guia_1102.circ as structural Verilog: 1 circuit, main circuit main
module main (
  input  x,
  input  clk,
  input  reset,
  output y
);

  Register #(.width(2)) register_1 ();  // open: D, en, Q, clk, clr
  // AND_Gate and_1 is placed but not wired
endmodule
