// Logisim project Mealy_1101.circ as structural Verilog: 1 circuit, main circuit main
module main (
  input  x,
  input  clk,
  input  reset,
  output y
);

  wire not_1_out, undriven, undriven_2;

  // NOT_Gate not_1 has open pins: in=open, out=not_1_out
  // AND_Gate and_1 has open pins: in4=undriven, out=open
  // AND_Gate and_2 has open pins: in0=undriven, in3=not_1_out, out=open
  // AND_Gate and_3 has open pins: in2=undriven_2, out=open
  // AND_Gate and_4 has open pins: in0=undriven_2, out=open
  // OR_Gate or_1 is placed but not wired
  Register #(.width(2)) register_1 ();  // open: D, en, Q, clk, clr
  // OR_Gate or_2 is placed but not wired
  // NOT_Gate not_2 is placed but not wired
  // AND_Gate and_5 is placed but not wired
endmodule
