// Logisim project Moore_1101.circ as structural Verilog: 1 circuit, main circuit main
module main (
  input  x,
  input  clk,
  input  reset,
  output y
);

  // AND_Gate and_1 is placed but not wired
  Register #(.width(3)) register_1 ();  // open: D, en, Q, clk, clr
  // OR_Gate or_1 is placed but not wired
  // OR_Gate or_2 is placed but not wired
  // NOT_Gate not_1 is placed but not wired
  // AND_Gate and_2 is placed but not wired
endmodule
