// Logisim project Guia_1201.circ as structural Verilog: 3 circuits
module jk_ff (
  input  j,
  input  k,
  input  clk,
  input  rst,
  output q
);

  // JK_Flip_Flop jk_ff_1: pin names not known; wires that end beside it: j, k, clk, rst, q
endmodule

module ram_1bit_cell (
  input  d,
  input  cs,
  input  rw,
  input  clk,
  input  rst,
  output q
);

  // NOT_Gate not_1 is placed but not wired
  // AND_Gate and_1 is placed but not wired
  // JK_Flip_Flop #(.trigger("falling")) jk_ff_1: pin names not known; wires that end beside it: d, cs, rw, clk, rst, q
  // AND_Gate and_2 is placed but not wired
endmodule

module main (
  input  [3:0] d_in,
  input  cs,
  input  rw,
  input  clk,
  input  rst,
  output [3:0] d_out
);

  wire undriven, undriven_2, undriven_3, undriven_4, undriven_5, undriven_6, undriven_7;

  ram_1bit_cell ram_1bit_cell_1 (.rw(undriven), .clk(undriven_2), .rst(undriven_3));  // open: d, cs, q
  ram_1bit_cell ram_1bit_cell_2 (
    .d(undriven), .cs(undriven_2), .rw(undriven_3), .clk(undriven_4), .rst(undriven_5));  // open: q
  ram_1bit_cell ram_1bit_cell_3 (
    .d(undriven_3), .cs(undriven_4), .rw(undriven_5), .clk(undriven_6), .rst(undriven_7));  // open: q
  ram_1bit_cell ram_1bit_cell_4 (.d(undriven_5), .cs(undriven_6), .rw(undriven_7));  // open: clk, rst, q
endmodule
