// Logisim project Guia_1202.circ as structural Verilog: 1 circuit, main circuit main
module main (
  input  [3:0] d_in,
  input  addr,
  input  cs,
  input  rw,
  input  clk,
  input  rst,
  output [3:0] d_out
);

  Demultiplexer demultiplexer_1 ();  // open: out0, out1, in, sel, en
  main main_1 ();  // open: d_in, addr, cs, rw, clk, rst, d_out
  main main_2 ();  // open: d_in, addr, cs, rw, clk, rst, d_out
  Multiplexer #(.width(4)) multiplexer_1 ();  // open: in0, in1, out, sel, en
endmodule
