// Logisim project Guia_1203.circ as structural Verilog: 1 circuit, main circuit main
module main (
  input  [7:0] d_in,
  input  addr,
  input  cs,
  output [7:0] d_out
);

  Demultiplexer demultiplexer_1 ();  // open: out0, out1, in, sel, en
  main main_1 ();  // open: d_in, addr, cs, d_out
  main main_2 ();  // open: d_in, addr, cs, d_out
  main main_3 ();  // open: d_in, addr, cs, d_out
  main main_4 ();  // open: d_in, addr, cs, d_out
  Multiplexer #(.width(4)) multiplexer_1 ();  // open: in0, in1, out, sel, en
  Multiplexer #(.width(4)) multiplexer_2 ();  // open: in0, in1, out, sel, en
endmodule
