// Logisim project Guia_1205.circ as structural Verilog: 1 circuit, main circuit main
module main (
);

  // Pin d_in: pin names not known
  // Pin addr: pin names not known
  // Splitter splitter_1: pin names not known
  // Pin cs: pin names not known
  // Demultiplexer demultiplexer_1: pin names not known
  main main_1 ();
  main main_2 ();
  // Multiplexer multiplexer_1: pin names not known
  // Pin d_out: pin names not known
endmodule
