// Logisim project Recuperacao_0203.circ as structural Verilog: 1 circuit, main circuit main
module main (
  output Q1,
  output Q2,
  output Q3
);

  wire clk1_padrao_out;

  Clock clk1_padrao (.out(clk1_padrao_out));
  // JK_Flip_Flop jk_ff_1: pin names not known; wires that end beside it: clk1_padrao_out, 1'b1, Q1
  // JK_Flip_Flop jk_ff_2: pin names not known; wires that end beside it: Q2
  // JK_Flip_Flop jk_ff_3: pin names not known; wires that end beside it: Q3
endmodule
