// Logisim project ULAA.circ as structural Verilog
module main (
  input  in_1,
  input  in_2,
  input  in_3,
  output out_4,
  output out_5
);

  // AND_Gate and_1 has open pins: in0=in_2, in1=in_3, out=open
  // OR_Gate or_1 has open pins: in0=in_2, in1=in_3, out=open
  // NOT_Gate not_1 has open pins: in=in_2, out=open
  somador somador_1 (.in_1(in_2), .in_2(in_3), .in_3(in_1), .out_5(out_5));  // open: out_4
endmodule

module meio (
  input  in_1,
  input  in_2,
  output out_3,
  output out_4
);

  xor xor_1 (out_3, in_1, in_2);
  and and_1 (out_4, in_1, in_2);
endmodule

module somador (
  input  in_1,
  input  in_2,
  input  in_3,
  output out_4,
  output out_5
);

  wire meio_1_out_3, meio_1_out_4, meio_2_out_4;

  meio meio_1 (.in_1(in_1), .in_2(in_2), .out_3(meio_1_out_3), .out_4(meio_1_out_4));
  meio meio_2 (.in_1(meio_1_out_3), .in_2(in_3), .out_3(out_4), .out_4(meio_2_out_4));
  or or_1 (out_5, meio_2_out_4, meio_1_out_4);
endmodule
